# Fritzing sketch wifi_robot_car_dWyN5trVCL (saved by Fritzing 0.9.3b)

parts:
  Part1 = Arduino Uno (Rev3)
  S1 = H-Bridge with L298N
  M1 = DC Motor
  M2 = DC Motor
  S2 = H-Bridge with L298N
  M3 = DC Motor
  M4 = DC Motor
  S4 = Square Pushbutton
  S3 = Square Pushbutton
  VCC1 = Battery block 9V
  J1 = Piezo Speaker
  R1 = Resistor [tolerance=±5% resistance=220 package="2010 [SMD]"]
  R2 = Resistor [tolerance=±5% resistance=220 package="2010 [SMD]"]
  Front_Left_Light = LEDs [package=led10mm]
  LED1 = LEDs [package=led10mm]
  U1 = NodeMCU V1.0

nets:
  N1: Part1.A0, R1.Pin_0
  N2: Part1.A1, R2.Pin_0
  N3: Part1.A4/SDA, J1.pin2
  N4: Part1.D8, S1.IN1
  N5: Part1.D9_PWM, S1.IN2
  N6: Part1.D10_PWM/SS, S1.ENA
  N7: Part1.D11_PWM/MOSI, S1.ENB
  N8: Part1.D12/MISO, S1.IN3
  N9: Part1.D13/SCK, S1.IN4
  GND: Part1.GND, J1.pin1, Front_Left_Light.C, LED1.C, U1.GND
  N10: Part1.D0/RX, U1.TX
  N11: Part1.D1/TX, U1.RX
  N12: Part1.D2, S2.IN1
  N13: Part1.D3_PWM, S2.IN2
  N14: Part1.D4, S2.IN3
  N15: Part1.D5_PWM, S2.ENA
  N16: Part1.D6_PWM, S2.ENB
  N17: Part1.D7, S2.IN4
  5V: Part1.5V, U1.Vin
  12V: S1.12V, S2.12V, S3.leg1
  GND_2: S1.GND, S2.GND, VCC1.-
  N18: S1.M1-01, M1.pin_2
  N19: S1.M1-02, M1.pin_1
  N20: S1.M2-01, M2.pin_2
  N21: S1.M2-02, M2.pin_1
  N22: S2.M1-01, M3.pin_2
  N23: S2.M1-02, M3.pin_1
  N24: S2.M2-01, M4.pin_2
  N25: S2.M2-02, M4.pin_1
  N26: S4.leg0, S3.leg0, VCC1.+

notes:
  Front Right Motor
  Back Right Motor
  Front Left Motor
  Back Left Motor
  Motors & Drivers Switch
  Arduino Switch
  NodeMCU V1.0
  Front Lights
  Buzzer

custom parts:
  H-Bridge with L298N: h-bridge
  NodeMCU V1.0: ESP8266 based NodeMCU
