# Fritzing sketch bt_car_3GVQE6rHXo (saved by Fritzing 0.9.2b)

parts:
  Part1 = Arduino Uno (Rev3)
  S1 = H-Bridge with L298N
  M1 = DC Motor
  M2 = DC Motor
  S2 = H-Bridge with L298N
  M3 = DC Motor
  M4 = DC Motor
  S4 = Square Pushbutton
  S3 = Square Pushbutton
  VCC1 = Battery block 9V
  Часть1 = Bluetooth HC-06
  LED1 = LEDs [package=led10mm]
  LED3 = smd LED [color="Red (633nm)" package="1206 [SMD]"]  # not connected
  LED4 = smd LED [color="Red (633nm)" package="1206 [SMD]"]
  J1 = Piezo Speaker
  R1 = Resistor [tolerance=±5% resistance=220 package="2010 [SMD]"]
  R2 = Resistor [tolerance=±5% resistance=220 package="2010 [SMD]"]
  R3 = Resistor [tolerance=±5% resistance=220 package="2010 [SMD]"]
  R4 = Resistor [tolerance=±5% resistance=220 package="2010 [SMD]"]
  Front_Left_Light = LEDs [package=led10mm]

nets:
  N1: Part1.A0, R1.Pin_0
  N2: Part1.A1, R2.Pin_0
  N3: Part1.A2, R4.Pin_1
  N4: Part1.A3, R3.Pin_1
  N5: Part1.A4/SDA, J1.pin2
  N6: Part1.D8, S1.IN1
  N7: Part1.D9_PWM, S1.IN2
  N8: Part1.D10_PWM/SS, S1.ENA
  N9: Part1.D11_PWM/MOSI, S1.ENB
  N10: Part1.D12/MISO, S1.IN3
  N11: Part1.D13/SCK, S1.IN4
  N12: Part1.D0/RX, Часть1.TXD
  N13: Part1.D1/TX, Часть1.RXD
  N14: Part1.D2, S2.IN1
  N15: Part1.D3_PWM, S2.IN2
  N16: Part1.D4, S2.IN3
  N17: Part1.D5_PWM, S2.ENA
  N18: Part1.D6_PWM, S2.ENB
  N19: Part1.D7, S2.IN4
  5V: Part1.5V, Часть1.VCC
  N20: Part1.GND, LED4.cathode, J1.pin1
  12V: S1.12V, S2.12V, S3.leg1
  GND: S1.GND, S2.GND, VCC1.-
  N21: S1.M1-01, M1.pin_2
  N22: S1.M1-02, M1.pin_1
  N23: S1.M2-01, M2.pin_2
  N24: S1.M2-02, M2.pin_1
  N25: S2.M1-01, M3.pin_2
  N26: S2.M1-02, M3.pin_1
  N27: S2.M2-01, M4.pin_2
  N28: S2.M2-02, M4.pin_1
  N29: S4.leg0, S3.leg0, VCC1.+
  N30: Часть1.GND, LED1.A, Front_Left_Light.A

notes:
  Front Right Motor
  Back Right Motor
  Front Left Motor
  Back Left Motor
  Motors & Drivers Switch
  Arduino Switch
  Bluetooth
  module
  HC-06
  Front Lights
  Buzzer
  Back Lights

custom parts:
  H-Bridge with L298N: h-bridge
